# Fritzing sketch StepperControl (saved by Fritzing 0.6.4b)
perfboards: 1

parts:
  Arduino1 = Arduino Mega
  Q1 = NPN-Transistor [part_number=2N2222 package="TO92 [THT]"]
  Q2 = NPN-Transistor [part_number=2N2222 package="TO92 [THT]"]
  Q3 = NPN-Transistor [part_number=2N2222 package="TO92 [THT]"]
  Q4 = NPN-Transistor [part_number=2N2222 package="TO92 [THT]"]
  D1 = Rectifier Diode [part_number=1N4001 package="300 mil [THT]"]
  D2 = Rectifier Diode [part_number=1N4001 package="300 mil [THT]"]
  D3 = Rectifier Diode [part_number=1N4001 package="300 mil [THT]"]
  D4 = Rectifier Diode [part_number=1N4001 package="300 mil [THT]"]

nets:
  N1: Arduino1.D5, Q4.B
  N2: Arduino1.D4, Q3.B
  N3: Arduino1.D3, Q2.B
  N4: Arduino1.D2, Q1.B
  N5: Q1.E, Q2.E, Q3.E
  N6: Q1.C, D1.anode
  N7: Q2.C, D2.anode
  N8: Q3.C, D3.anode
  N9: Q4.C, D4.anode
  N10: D1.cathode, D4.cathode
